// Logisim project FPA.circ as structural Verilog: 2 circuits, main circuit main
module main (
  input  [31:0] A,
  input  [31:0] B,
  output [31:0] Output,
  output Overflow,
  output Underflow
);

  wire input_1_larger_s_sign, input_1_smaller_s_sign, main_1_p6;
  wire [8:0] input_1_larger_exponent, normalizer_1_normalized_exponent;
  wire [10:0] rounded_normalizer_1_p3;
  wire [19:0] rounded_normalizer_1_p4_2;
  wire [31:0] input_1_larger_s_fraction, input_1_shifted_smaller_s_fraction, main_1_p5,
       normalizer_1_normalized_significand, rounded_normalizer_1_p4, rounder_1_rounded_significand;

  Input input_1 (
    .A(A), .B(B), .Larger_s_Fraction(input_1_larger_s_fraction), .Larger_s_Sign(input_1_larger_s_sign),
    .Larger_Exponent(input_1_larger_exponent),
    .Shifted_Smaller_s_Fraction(input_1_shifted_smaller_s_fraction), .Smaller_s_sign(input_1_smaller_s_sign));  // open: Exponent_Difference, Smaller_s_Fraction
  // adder32bit_main main_1: pin names not known; wires that end beside it: input_1_larger_s_sign, input_1_larger_s_fraction, input_1_shifted_smaller_s_fraction, input_1_smaller_s_sign, main_1_p5, main_1_p6
  normalizer normalizer_1 (
    .exponent_input(input_1_larger_exponent), .significand_input(main_1_p5), .underflow(Underflow),
    .overflow(Overflow), .normalized_Exponent(normalizer_1_normalized_exponent),
    .normalized_Significand(normalizer_1_normalized_significand));
  Rounder rounder_1 (
    .significand(normalizer_1_normalized_significand), .rounded_significand(rounder_1_rounded_significand));
  OutputHandler outputhandler_1 (
    .Significand(rounded_normalizer_1_p4_2), .exponent(rounded_normalizer_1_p3), .S(main_1_p6),
    .Output(Output));
  // rounded_normalizer rounded_normalizer_1: pin names not known; wires that end beside it: normalizer_1_normalized_exponent, rounder_1_rounded_significand, rounded_normalizer_1_p3, {rounded_normalizer_1_p4[31:30], rounded_normalizer_1_p4_2, rounded_normalizer_1_p4[9:0]}
endmodule

// OpH
module OutputHandler (
  input  [19:0] Significand,
  input  [10:0] exponent,
  input  S,
  output [31:0] Output
);


  assign Output = {S, exponent, Significand};
endmodule
