// Logisim project rightShifterMax.circ as structural Verilog: 1 circuit, main circuit rightShifter
// RS
module rightShifter (
  input  [31:0] Significand,
  input  [8:0] Exponent_Difference,
  output [31:0] Output
);

  wire or_1_out;
  wire [31:0] arbitary_rightshifter_1_p3;

  // arbitary_rightShifter arbitary_rightshifter_1: pin names not known; wires that end beside it: Significand, Exponent_Difference[4:0], arbitary_rightshifter_1_p3
  or or_1 (or_1_out, Exponent_Difference[8], Exponent_Difference[7], Exponent_Difference[6], Exponent_Difference[5]);
  Multiplexer #(.width(32)) multiplexer_1 (
    .in0(arbitary_rightshifter_1_p3), .in1({32{1'b0}}), .out(Output), .sel(or_1_out), .en(1'b1));
endmodule
