// Logisim project rounder.circ as structural Verilog: 1 circuit, main circuit Rounder
// RNDR
module Rounder (
  input  [31:0] significand,
  output [31:0] rounded_significand
);

  wire and_1_out, comparator_1_eq, comparator_1_gt, or_1_out;

  Comparator #(.width(10), .mode("unsigned")) comparator_1 (
    .a(significand[9:0]), .b(10'h200), .gt(comparator_1_gt), .eq(comparator_1_eq));  // open: lt
  and and_1 (and_1_out, significand[10], comparator_1_eq);
  Adder #(.width(22)) adder_1 (
    .a(significand[31:10]), .b({22{1'b0}}), .out(rounded_significand[31:10]), .cin(or_1_out));  // open: cout
  or or_1 (or_1_out, and_1_out, comparator_1_gt);

  assign rounded_significand[9:0] = {10{1'b0}};
endmodule
