// Logisim project zero-checker-significand.circ as structural Verilog: 1 circuit, main circuit zero-checker-significand
// ZCS
module zero_checker_significand (
  input  [21:0] Significand,
  output out_2
);

  nor nor_1 (out_2, Significand[0], Significand[1], Significand[2], Significand[3], Significand[4], Significand[5], Significand[6], Significand[7], Significand[8], Significand[9], Significand[10], Significand[12], Significand[13], Significand[14], Significand[15], Significand[16], Significand[17], Significand[18], Significand[19], Significand[20], Significand[21], Significand[11]);
endmodule
